# Fritzing sketch Montage sonar vibreur (saved by Fritzing 0.9.3b)
breadboards: 1

parts:
  Q1 = PNP-Transistor [package="TO92 [THT]"]  # not connected
  U1 = Vibration Motor- ROB-08449 [package=vibe-motor-10mm]
  Part1 = Arduino Uno (Rev3)
  U3 = SEN-00639 Ultrasonic range finder [chip_label=? package=THT]

nets:
  GND: U1.+, Part1.GND, U3.GND
  N1: Part1.D10_PWM/SS, U3.Trig
  N2: Part1.5V, U3.+5

custom parts:
  SEN-00639 Ultrasonic range finder: Ultrasonic range finder
